# Fritzing sketch Untitled Sketch (saved by Fritzing 0.9.3b)
breadboards: 1

parts:
  Componente1 = Arduino Uno (Rev3)  # not connected
  Componente2 = Arduino Uno (Rev3)
  R1 = Photocell (LDR) [package=THT]
  R2 = Resistor [tolerance=±5% resistance=220 package=THT]
  R3 = Resistor [tolerance=±5% resistance=220 package=THT]
  R4 = Resistor [tolerance=±5% resistance=220 package=THT]
  LED1 = LED - 5mm [color="Blue (525nm)" package="5 mm [THT]"]
  LED2 = LED - 5mm [color="Blue (525nm)" package="5 mm [THT]"]

nets:
  N1: Componente2.A0, R1.pin_0, R2.Pin_1
  N2: Componente2.D13/SCK, LED1.anode
  N3: Componente2.GND, R2.Pin_0, R4.Pin_1
  N4: Componente2.5V, R1.pin_1
  N5: R3.Pin_0, LED1.cathode
  N6: R3.Pin_1, LED2.anode
  N7: R4.Pin_0, LED2.cathode
